# Fritzing sketch SimpleCounter (saved by Fritzing 0.7.4b)
breadboards: 1

parts:
  Arduino1 = Arduino
  R1 = Resistor [tolerance=±5% resistance=0 package=THT]
  7_Segment1 = 7 Segment Display

nets:
  N1: Arduino1.GND, R1.Pin_1
  N2: Arduino1.D10, 7_Segment1.Segment_A
  N3: Arduino1.D9, 7_Segment1.Segment_B
  N4: Arduino1.D5, 7_Segment1.Segment_D
  N5: Arduino1.D4, 7_Segment1.Segment_E
  N6: Arduino1.D2, 7_Segment1.Segment_F
